# Fritzing sketch fire fighting robot (saved by Fritzing 0.9.3b)

parts:
  Part1 = Arduino Uno (Rev3) - ICSP
  Part2 = Rotoshield - Motor driver shield for Arduino
  M1 = DC Motor
  M2 = DC Motor
  M3 = DC Motor
  M4 = DC Motor
  Mod1 = KY-026 Flame Sensor Module [package="Breakout board"]
  Mod2 = KY-026 Flame Sensor Module [package="Breakout board"]
  Mod3 = KY-026 Flame Sensor Module [package="Breakout board"]
  Mod4 = KY-019 5V Relay Module [package="Breakout board"]
  WATER_PUMP1 = water pump/motor
  VCC1 = 4 x AAA Battery Mount
  J1 = Basic Servo

nets:
  N1: Part1.A0, Part2.A_IN_0, Mod1.A0
  N2: Part1.A1, Part2.A_IN_1, Mod3.A0
  N3: Part1.A2, Part2.A_IN_2, Mod2.A0
  N4: Part1.A3, Part2.A_IN_3
  N5: Part1.A4/SDA, Part2.A_IN_4, Mod4.S
  N6: Part1.A5/SCL, Part2.A_IN_5
  N7: Part1.ICSP_MOSI, Part1.D11_PWM/MOSI, Part2.DIG_11
  N8: Part1.D8, Part2.DIG_8
  N9: Part1.D9_PWM, Part2.DIG_9, J1.pulse
  N10: Part1.D10_PWM/SS, Part2.DIG_10
  N11: Part1.D12/MISO, Part2.DIG_12
  N12: Part1.D13/SCK, Part2.DIG_13
  GND: Part1.GND, Part2.GND, Mod3.G, Mod4.-, WATER_PUMP1.pin_1, VCC1.-, J1.gnd
  N13: Part1.AREF, Part2.AREF
  N14: Part1.D0/RX, Part2.DIG_0
  N15: Part1.D1/TX, Part2.DIG_1
  N16: Part1.D2, Part2.DIG_2
  N17: Part1.D3_PWM, Part2.DIG_3
  N18: Part1.D4, Part2.DIG_4
  N19: Part1.D5_PWM, Part2.DIG_5
  N20: Part1.D6_PWM, Part2.DIG_6
  N21: Part1.D7, Part2.DIG_7
  N22: Part1.RESET, Part2.RESET
  3V3: Part1.3V3, Part2.+3V3
  5V: Part1.5V, Part2.+5V, Mod1.+
  VIN: Part1.VIN, Part2.VIN
  N23: Part2.VCC, Mod4.Common, VCC1.+
  N24: Part2.M1-2, M3.pin_2
  N25: Part2.M1-1, M3.pin_1
  N26: Part2.M2-2, M4.pin_2
  N27: Part2.M2-1, M4.pin_1
  N28: Part2.M3-2, M1.pin_2
  N29: Part2.M3-1, M1.pin_1
  N30: Part2.M4-2, M2.pin_2
  N31: Part2.M4-1, M2.pin_1
  N32: Part2.2, Mod4.+
  N33: Part2.5, J1.vcc
  N34: Mod2.+, Mod3.+
  N35: Mod4.NC, WATER_PUMP1.pin_2

custom parts:
  KY-026 Flame Sensor Module: KY-026 Flame Sensor Module reacts in the presence of fire.
  KY-019 5V Relay Module: KY-019 5V Relay module, used to control AC circuits. (Special thanks to vanepp for fixing the PCB holes and other errors)
  water pump/motor: WATER PUMP BY ARDUBLOCKTR
